# Fritzing sketch picfancontrol-circuit-icsp (saved by Fritzing 0.9.3b)
breadboards: 1

parts:
  Q1 = Basic FET N-Channel [package="TO220 [THT]"]
  R1 = Resistor [tolerance=±5% resistance=2.2k package=THT]
  U1 = IC, DIP package, 8 pins [chip_label=PIC part_number=PIC12F675]
  J1 = female pin header, 5 pins [form="♀ (female)" part_number=ICSP]
  R2 = Temperature Sensor (Thermistor) [thermistor_type=NTC part_number="NTC 50K" package=THT]
  R3 = Resistor [tolerance=±5% resistance=47k package=THT]
  J2 = female pin header, 2 pins [form="♀ (female)" part_number=FAN]
  C1 = Ceramic Capacitor [capacitance=100nF package="100 mil [THT, multilayer]"]
  IC1 = Voltage Regulator [package=to-92]

nets:
  N1: Q1.gate, R1.Pin_0
  N2: Q1.drain, J2.pin2
  GND: Q1.source, R3.Pin_0, C1.0
  N3: R1.Pin_1, U1.pin2
  5V: U1.pin1, J1.pin2, R2.pin_1, C1.1, IC1.OUT
  N4: U1.pin4, J1.pin1
  N5: U1.pin5, R2.pin_0, R3.Pin_1
  N6: U1.pin6, J1.pin5
  N7: U1.pin7, J1.pin4
  N8: U1.pin8, J1.pin3, IC1.GND
  12V: J2.pin1, IC1.IN
