# Fritzing sketch picfancontrol-circuit-minimal (saved by Fritzing 0.9.3b)
circuit board: 1.69571cm x 3.26545cm
breadboards: 1

parts:
  Q1 = Basic FET N-Channel [package="TO220 [THT]"]
  R1 = Resistor [tolerance=±5% resistance=2.2k package=THT]
  U1 = IC, DIP package, 8 pins [chip_label=PIC part_number=PIC12F675]
  R3 = Resistor [tolerance=±5% resistance=47k package=THT]
  C1 = Ceramic Capacitor [capacitance=100nF package="100 mil [THT, multilayer]"]
  J2 = female pin header, 1 pin [form="♀ (female)" part_number=Fan]
  J3 = female pin header, 2 pins [form="♀ (female)" part_number=5V]
  R2 = Temperature Sensor (Thermistor) [thermistor_type=NTC part_number="NTC 50K" package=THT]

nets:
  N1: Q1.gate, R1.Pin_0
  N2: Q1.drain, J2.pin1
  GND: Q1.source, U1.pin8, R3.Pin_0, C1.0, J3.pin2
  N3: R1.Pin_1, U1.pin2
  5V: U1.pin1, C1.1, J3.pin1, R2.pin_1
  N4: U1.pin5, R3.Pin_1, R2.pin_0
