# Fritzing sketch picfancontrol-circuit (saved by Fritzing 0.9.3b)
circuit board: 4.83617cm x 1.72893cm
breadboards: 1

parts:
  R1 = Resistor [tolerance=±5% resistance=2.2k package=THT]
  R3 = Resistor [tolerance=±5% resistance=47k package=THT]
  Fan = female pin header, 2 pins [form="♀ (female)"]
  IC1 = Voltage Regulator [package=to-92]
  NTC2 = female pin header, 2 pins [form="♀ (female)"]
  NTC1 = female pin header, 2 pins [form="♀ (female)"]
  R4 = Resistor [tolerance=±5% resistance=47k package=THT]
  12V = female pin header, 2 pins [form="♀ (female)"]
  C1 = Ceramic Capacitor [capacitance=100nF package="100 mil [THT, multilayer]"]
  Q1 = Basic FET N-Channel [package="DPak [SMD]"]
  U1 = IC, DIP package, 8 pins [chip_label=PIC part_number=PIC12F675]

nets:
  N1: R1.Pin_0, Q1.Gate
  N2: R1.Pin_1, U1.pin2
  GND: R3.Pin_0, IC1.GND, R4.Pin_0, 12V.pin2, C1.1, Q1.source, U1.pin8
  N3: R3.Pin_1, NTC2.pin2, U1.pin5
  12V: Fan.pin1, IC1.IN, 12V.pin1
  N4: Fan.pin2, Q1.drain
  5V: IC1.OUT, NTC2.pin1, NTC1.pin1, C1.0, U1.pin1
  N5: NTC1.pin2, R4.Pin_1, U1.pin6
